# Fritzing sketch BatteryManagementSystem (saved by Fritzing 0.9.3b)
breadboards: 2

parts:
  R1 = Resistor [tolerance=±5% resistance=3.3k package="0402 [SMD]"]
  BAT7 = Battery Holders [package=battery-aa]
  BAT8 = Battery Holders [package=battery-aa]
  BAT9 = Battery Holders [package=battery-aa]
  BAT10 = Battery Holders [package=battery-aa]
  BAT11 = Battery Holders [package=battery-aa]
  BAT12 = Battery Holders [package=battery-aa]
  Part1 = Arduino Uno (Rev3)
  R2 = Resistor [tolerance=±5% resistance=4.7k package="0402 [SMD]"]
  R3 = Resistor [tolerance=±5% resistance=3.3k package="0402 [SMD]"]
  R4 = Resistor [tolerance=±5% resistance=10k package="0402 [SMD]"]
  R5 = Resistor [tolerance=±5% resistance=3.3k package="0402 [SMD]"]
  R6 = Resistor [tolerance=±5% resistance=16k package="0402 [SMD]"]
  R7 = Resistor [tolerance=±5% resistance=3.3k package="0402 [SMD]"]
  R8 = Resistor [tolerance=±5% resistance=3.3k package="0402 [SMD]"]
  R9 = Resistor [tolerance=±5% resistance=3.3k package="0402 [SMD]"]
  R10 = Resistor [tolerance=±5% resistance=3.3k package="0402 [SMD]"]
  R11 = Resistor [tolerance=±5% resistance=3.3k package="0402 [SMD]"]
  R12 = Resistor [tolerance=±5% resistance=3.3k package="0402 [SMD]"]
  Part2 = Adafruit ADS1115 16Bit I2C ADC [part_number="Adafruit #1085"]
  Part3 = Adafruit ADS1115 16Bit I2C ADC [part_number="Adafruit #1085"]
  Part4 = Adafruit ADS1115 16Bit I2C ADC [part_number="Adafruit #1085"]
  L1 = Inductor [package="400 mil [THT]"]
  DS1 = DS18B20 1-Wire Temperature Sensor [part_number=DS18B20]
  DS2 = DS18B20 1-Wire Temperature Sensor [part_number=DS18B20]
  DS3 = DS18B20 1-Wire Temperature Sensor [part_number=DS18B20]
  DS4 = DS18B20 1-Wire Temperature Sensor [part_number=DS18B20]
  DS5 = DS18B20 1-Wire Temperature Sensor [part_number=DS18B20]
  DS6 = DS18B20 1-Wire Temperature Sensor [part_number=DS18B20]
  R13 = Resistor [tolerance=±5% resistance=4.7k package=THT]
  R14 = Resistor [tolerance=±5% resistance=33 package=THT]
  R15 = Resistor [tolerance=±5% resistance=10k package=THT]
  R16 = Resistor [tolerance=±5% resistance=10k package=THT]
  C2 = Electrolytic Capacitor [capacitance=10µF package="1010 [SMD, electrolytic]"]

nets:
  N1: R1.Pin_0, R2.Pin_1, Part3.AIN2, Part3.AIN1
  N2: R1.Pin_1, BAT8.+, R3.Pin_1, R5.Pin_1, R7.Pin_1, R8.Pin_1, R9.Pin_1, Part3.AIN0
  N3: BAT7.-, BAT10.+, R10.Pin_0
  N4: BAT7.+, BAT12.-, R6.Pin_0
  N5: BAT8.-, BAT9.+, R2.Pin_0
  N6: BAT9.-, BAT12.+, R4.Pin_0
  N7: BAT10.-, BAT11.+, R11.Pin_0
  N8: BAT11.-, R12.Pin_0
  N9: Part1.A0, L1.pin_0, R14.Pin_0
  N10: Part1.A4/SDA, Part2.SDA, Part3.SDA, Part4.ADDR, Part4.SDA
  N11: Part1.A5/SCL, Part2.SCL, Part3.SCL, Part4.SCL
  GND: Part1.GND, Part2.GND, Part3.GND, Part4.GND, DS1.GND, DS2.GND, DS3.GND, DS4.GND, DS5.GND, DS6.GND, R16.Pin_1, C2.-
  N12: Part1.D2, DS1.DQ, DS2.DQ, DS3.DQ, DS4.DQ, DS5.DQ, DS6.DQ, R13.Pin_0
  VDD: Part1.5V, Part2.ADDR, Part2.VDD, Part3.VDD, Part4.VDD, DS1.VDD, DS2.VDD, DS3.VDD, DS4.VDD, DS5.VDD, DS6.VDD, R13.Pin_1, R15.Pin_0
  N13: R3.Pin_0, R4.Pin_1, Part2.AIN0, Part3.AIN3
  N14: R5.Pin_0, R6.Pin_1, Part2.AIN2, Part2.AIN1
  N15: R7.Pin_0, R10.Pin_1, Part2.AIN3, Part4.AIN0
  N16: R8.Pin_0, R11.Pin_1, Part4.AIN2, Part4.AIN1
  N17: R9.Pin_0, R12.Pin_1, Part4.AIN3
  N18: L1.pin_1, R14.Pin_1, R15.Pin_1, R16.Pin_0, C2.+

custom parts:
  Adafruit ADS1115 16Bit I2C ADC: For microcontrollers without an analog-to-digital converter or when you want a higher-precision ADC, the ADS1115 provides 16-bit precision at 860 samples/second over I2C. The chip can be configured as 4 single-ended input channels, or two differential channels. As a nice bonus, it even includes a programmable gain amplifier, up to x16, to help boost up smaller single/differential signals to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
